# Fritzing sketch portal gun (saved by Fritzing 0.8.7b)
breadboards: 1

parts:
  Part1 = Arduino Nano (Rev3.0) (ICSP)
  Part2 = Adafruit Audio FX Mini Sound Board [part_number="Adafruit #2342 and #2220"]
  Center_Lights = NeoPixel Jewel [part_number=2226]
  LED2 = LED - 5mm [color="Red (633nm)" package="5 mm [THT]"]
  LED3 = LED - 5mm [color="Red (633nm)" package="5 mm [THT]"]
  LED4 = LED - 5mm [color="Red (633nm)" package="5 mm [THT]"]
  Song_Button = Square Pushbutton
  Cancel_Button = Square Pushbutton
  Indicator_Light = prefix0000
  Power_up/down_Switch = SPST Switch [package=r_sw_th]
  End_Lights = NeoPixel Jewel [part_number=2226]
  R1 = Resistor [tolerance=±5% resistance=220 package=THT]
  R2 = Resistor [tolerance=±5% resistance=220 package=THT]
  R3 = Resistor [tolerance=±5% resistance=220 package=THT]
  Orange_Button = Waterproof Pushbutton (red)
  Blue_Button = Waterproof Pushbutton (blue)
  SP1 = SPEAKER [package=pcb_mount_speaker]
  SP2 = SPEAKER [package=pcb_mount_speaker]
  Micro_USB_port = Adafruit Micro USB Breakout [part_number="Adafruit #1833"]
  AMP1 = GF1002 Stereo Amplifier
  Part4 = 16 NeoPixel Ring [part_number=1463]
  Main_Power_Switch = SPST Switch [package=r_sw_th]

nets:
  GND: Part1.GND, Part2.GND, Part2.UG, Center_Lights.GND, LED2.cathode, LED3.cathode, LED4.cathode, Song_Button.leg1, Cancel_Button.leg1, Indicator_Light.connector3, Power_up/down_Switch.S, End_Lights.GND, Orange_Button.no_name_yet#1, Orange_Button.no_name_yet#5, Blue_Button.no_name_yet#1, Blue_Button.no_name_yet#5, Micro_USB_port.GND, AMP1.POWER-, AMP1.INPUTG, Part4.GND
  N1: Part1.D2, Indicator_Light.connector2
  N2: Part1.D5, Song_Button.leg0
  N3: Part1.D6, Power_up/down_Switch.P
  N4: Part1.D7, Blue_Button.no_name_yet#2
  N5: Part1.D8, Orange_Button.no_name_yet#2
  N6: Part1.D9, Cancel_Button.leg0
  N7: Part1.D10, Part2.RST
  N8: Part1.D11/MOSI, Part2.RX_5V
  N9: Part1.D12/MISO, Part2.TX
  VDD: Part1.5V, Part2.VIN, Center_Lights.VDD, Indicator_Light.connector1, End_Lights.VDD, AMP1.POWER+, Part4.VDD, Main_Power_Switch.S
  N10: Part1.A2, Orange_Button.no_name_yet#4
  N11: Part1.A1, Blue_Button.no_name_yet#4
  N12: Part1.A0, R1.Pin_1, R2.Pin_1, R3.Pin_1
  N13: Part1.D13/SCK, Part2.ACT
  N14: Part2.R_AC, AMP1.INPUTR
  N15: Part2.L_AC, AMP1.INPUTL
  N16: Center_Lights.IN, Indicator_Light.connector4
  N17: Center_Lights.OUT, End_Lights.IN
  N18: LED2.anode, R2.Pin_0
  N19: LED3.anode, R1.Pin_0
  N20: LED4.anode, R3.Pin_0
  N21: End_Lights.OUT, Part4.IN
  N22: SP1.+, AMP1.LOUT-
  N23: SP1.-, AMP1.LOUT+
  N24: SP2.+, AMP1.ROUT-
  N25: SP2.-, AMP1.ROUT+
  N26: Micro_USB_port.VBUS, Main_Power_Switch.P

notes:
  Ring Center Indicator
  Cancel Song
  Power up/down Switch
  Main Power Switch

custom parts:
  Adafruit Audio FX Mini Sound Board: Would you like to add audio/sound effects to your next project, without an Arduino+Shield? Or maybe you don't even know how to use microcontrollers, you just want to make a sound play whenever you press a button. What about something that has to be very small and portable? You are probably feeling a little frustrated: it's been very hard to find a simple, low cost audio effects trigger that is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
  NeoPixel Jewel: We fit seven of our tiny 5050 (5mm x 5mm) smart RGB LEDs onto a beautiful, round PCB with mounting holes and a chainable design to create what we think is our most elegant (and evening-wear appropriate) NeoPixel board yet. Use only one microcontroller pin to control as many as you can chain together! Each LED is addressable as the driver chip is inside the LED. Each one has ~18mA constant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
  Waterproof Pushbutton (red): Waterproof Illuminated Pushbutton (red)
  Waterproof Pushbutton (blue): Waterproof Illuminated Pushbutton (blue)
  Adafruit Micro USB Breakout: Simple but effective - this breakout board has a USB Micro-B connector, with all 5 pins broken out. Great for pairing with a microcontroller with USB support, or adding USB 5V power to a project. We use a micro-AB connector with through-hole shielding pads for an excellent strong connection - it won't rip off by accident! Comes with one fully assembled and tested micro B breakout PCB and a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
  GF1002 Stereo Amplifier: GF1002 6 Watt Stereo Amplifier
  16 NeoPixel Ring: 16 ultra bright smart LED NeoPixels are arranged in a circle with 1.75" (44.5mm) outer diameter. The rings are 'chainable' - connect the output pin of one to the input pin of another. Use only one microcontroller pin to control as many as you can chain together! Each LED is addressable as the driver chip is inside the LED. Each one has ~18mA constant current drive so the color will be very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
